// Logisim project Decodificador.circ as structural Verilog: 2 circuits, main circuit decodificador
// decc
module decodificador (
  input  A,
  input  B,
  input  C,
  input  D,
  output a_2,
  output b_2,
  output c_2,
  output d_2,
  output e,
  output f,
  output g,
  output sinal
);

  wire and_1_out, and_2_out, and_3_out, and_4_out, and_5_out, and_6_out, and_7_out, and_8_out, and_9_out,
       and_10_out, and_11_out, and_12_out, and_13_out, and_14_out, and_15_out, and_16_out, and_17_out,
       and_18_out, and_19_out, and_20_out, and_21_out, and_22_out, and_23_out, and_24_out, and_25_out,
       and_26_out, and_27_out, and_28_out, not_1_out, not_2_out, not_3_out, not_4_out;

  not not_1 (not_1_out, A);
  not not_2 (not_2_out, B);
  not not_3 (not_3_out, C);
  not not_4 (not_4_out, D);
  and and_1 (and_1_out, not_2_out, A);
  and and_2 (and_2_out, C, not_4_out);
  and and_3 (and_3_out, not_4_out, not_2_out);
  and and_4 (and_4_out, not_1_out, C);
  and and_5 (and_5_out, B, not_3_out, D);
  and and_6 (and_6_out, not_2_out, not_1_out);
  and and_7 (and_7_out, B, A);
  and and_8 (and_8_out, not_3_out, not_4_out);
  and and_9 (and_9_out, not_3_out, A);
  and and_10 (and_10_out, D, C, not_1_out);
  buf and_11 (and_11_out, not_3_out);  // AND_Gate
  buf and_12 (and_12_out, D);  // AND_Gate
  and and_13 (and_13_out, B, not_1_out);
  and and_14 (and_14_out, not_2_out, A);
  and and_15 (and_15_out, not_4_out, C);
  and and_16 (and_16_out, C, not_2_out);
  and and_17 (and_17_out, not_4_out, not_2_out);
  and and_18 (and_18_out, D, not_3_out, B);
  and and_19 (and_19_out, not_4_out, C);
  and and_20 (and_20_out, not_2_out, not_4_out);
  and and_21 (and_21_out, not_4_out, not_3_out);
  and and_22 (and_22_out, not_2_out, C, A);
  and and_23 (and_23_out, not_3_out, not_3_out, B, not_1_out);
  and and_24 (and_24_out, not_4_out, B, not_1_out);
  and and_25 (and_25_out, not_4_out, C);
  and and_26 (and_26_out, not_3_out, B);
  and and_27 (and_27_out, not_4_out, A);
  and and_28 (and_28_out, C, not_2_out);
  or or_1 (a_2, and_1_out, and_2_out, and_3_out, and_4_out, and_5_out);
  or or_2 (b_2, and_6_out, and_7_out, and_8_out, and_9_out, and_10_out);
  or or_3 (c_2, and_11_out, and_12_out, and_13_out, and_14_out);
  or or_4 (d_2, and_15_out, and_16_out, and_17_out, and_18_out);
  or or_5 (e, and_19_out, and_20_out);
  or or_6 (f, and_21_out, and_22_out, and_23_out, and_24_out);
  or or_7 (g, and_25_out, and_26_out, and_27_out, and_28_out);
  buf or_8 (sinal, A);  // OR_Gate
endmodule

module principal (
  input  A,
  input  B,
  input  C,
  input  D
);

  wire decodificador_1_a_2, decodificador_1_b_2, decodificador_1_c_2, decodificador_1_d_2, decodificador_1_e,
       decodificador_1_f, decodificador_1_g, decodificador_1_sinal;

  decodificador decodificador_1 (
    .A(A), .B(B), .C(C), .D(D), .a_2(decodificador_1_a_2), .b_2(decodificador_1_b_2),
    .c_2(decodificador_1_c_2), .d_2(decodificador_1_d_2), .e(decodificador_1_e), .f(decodificador_1_f),
    .g(decodificador_1_g), .sinal(decodificador_1_sinal));
  _7_Segment_Display u_7_segment_display_1 (
    .g(decodificador_1_g), .f(decodificador_1_f), .a(decodificador_1_a_2), .b(decodificador_1_b_2),
    .e(decodificador_1_e), .d(decodificador_1_d_2), .c(decodificador_1_c_2));  // open: dp
  _7_Segment_Display u_7_segment_display_2 (.g(decodificador_1_sinal));  // open: f, a, b, e, d, c, dp
endmodule
