// Logisim project Atividade 2 - Charlies Augusto Sichelero.circ as structural Verilog: 10 circuits, main circuit sin
module sin (
  input  A,
  input  B,
  input  C,
  input  D,
  output sin
);


  assign sin = A;
endmodule

module a (
  input  A,
  input  B,
  input  C,
  input  D,
  output a_2
);

  wire and_1_out, and_2_out, and_3_out, and_4_out, and_5_out, not_1_out, not_2_out, not_3_out, not_4_out;

  not not_1 (not_1_out, A);
  not not_2 (not_2_out, C);
  not not_3 (not_3_out, B);
  not not_4 (not_4_out, D);
  and and_1 (and_1_out, A, not_3_out);
  and and_2 (and_2_out, C, not_4_out);
  and and_3 (and_3_out, not_3_out, not_4_out);
  and and_4 (and_4_out, not_1_out, C);
  and and_5 (and_5_out, B, not_2_out, D);
  or or_1 (a_2, and_1_out, and_2_out, and_3_out, and_4_out, and_5_out);
endmodule

module b (
  input  A,
  input  B,
  input  C,
  input  D,
  output b_2
);

  wire and_1_out, and_2_out, and_3_out, and_4_out, not_1_out, not_2_out, not_3_out, not_4_out;

  not not_1 (not_1_out, A);
  not not_2 (not_2_out, C);
  not not_3 (not_3_out, B);
  not not_4 (not_4_out, D);
  and and_1 (and_1_out, not_2_out, not_4_out);
  and and_2 (and_2_out, not_1_out, B, not_2_out);
  and and_3 (and_3_out, not_1_out, B, not_4_out);
  and and_4 (and_4_out, A, not_3_out, C);
  or or_1 (b_2, and_1_out, and_2_out, and_3_out, and_4_out);
endmodule

module c (
  input  A,
  input  B,
  input  C,
  input  D,
  output c_2
);

  wire and_1_out, and_2_out, not_1_out, not_2_out, not_3_out;

  not not_1 (not_1_out, C);
  not not_2 (not_2_out, B);
  not not_3 (not_3_out, D);
  and and_1 (and_1_out, not_1_out, not_2_out, not_3_out);
  and and_2 (and_2_out, C, not_3_out);
  or or_1 (c_2, and_1_out, and_2_out);
endmodule

module d (
  input  A,
  input  B,
  input  C,
  input  D,
  output d_2
);

  wire and_1_out, and_2_out, and_3_out, and_4_out, not_1_out, not_2_out, not_3_out;

  not not_1 (not_1_out, C);
  not not_2 (not_2_out, B);
  not not_3 (not_3_out, D);
  and and_1 (and_1_out, not_2_out, not_1_out, not_3_out);
  and and_2 (and_2_out, B, not_1_out, D);
  and and_3 (and_3_out, not_2_out, C);
  and and_4 (and_4_out, C, not_3_out);
  or or_1 (d_2, and_1_out, and_2_out, and_3_out, and_4_out);
endmodule

module e (
  input  A,
  input  B,
  input  C,
  input  D,
  output e
);

  wire and_1_out, and_2_out, not_1_out, not_2_out, not_3_out;

  not not_1 (not_1_out, A);
  not not_2 (not_2_out, C);
  not not_3 (not_3_out, B);
  and and_1 (and_1_out, not_1_out, B);
  and and_2 (and_2_out, A, not_3_out);
  or or_1 (e, not_2_out, D, and_1_out, and_2_out);
endmodule

module f (
  input  A,
  input  B,
  input  C,
  input  D,
  output f
);

  wire and_1_out, and_2_out, and_3_out, and_4_out, and_5_out, not_1_out, not_2_out, not_3_out, not_4_out;

  not not_1 (not_1_out, A);
  not not_2 (not_2_out, C);
  not not_3 (not_3_out, B);
  not not_4 (not_4_out, D);
  and and_1 (and_1_out, not_1_out, not_3_out);
  and and_2 (and_2_out, not_2_out, not_4_out);
  and and_3 (and_3_out, A, B);
  and and_4 (and_4_out, B, C, D);
  and and_5 (and_5_out, A, not_3_out, not_2_out);
  or or_1 (f, and_1_out, and_2_out, and_3_out, and_4_out, and_5_out);
endmodule

module g (
  input  A,
  input  B,
  input  C,
  input  D,
  output g
);

  wire and_1_out, and_2_out, and_3_out, and_4_out, not_2_out, not_3_out, not_4_out;

  // NOT_Gate not_1 has open pins: in=A, out=open
  not not_2 (not_2_out, B);
  not not_3 (not_3_out, C);
  not not_4 (not_4_out, D);
  and and_1 (and_1_out, B, not_3_out);
  and and_2 (and_2_out, A, not_3_out, not_4_out);
  and and_3 (and_3_out, not_2_out, C, D);
  and and_4 (and_4_out, C, not_4_out);
  or or_1 (g, and_1_out, and_2_out, and_3_out, and_4_out);
endmodule

module Decodificador (
  input  A,
  input  B,
  input  C,
  input  D,
  output a_2,
  output b_2,
  output c_2,
  output d_2,
  output e,
  output f,
  output g,
  output sin
);

  b b_1 (.A(A), .B(B), .C(C), .D(D), .b_2(b_2));
  c c_1 (.A(A), .B(B), .C(C), .D(D), .c_2(c_2));
  f f_1 (.A(A), .B(B), .C(C), .D(D), .f(f));
  a a_1 (.A(A), .B(B), .C(C), .D(D), .a_2(a_2));
  d d_1 (.A(A), .B(B), .C(C), .D(D), .d_2(d_2));
  g g_1 (.A(A), .B(B), .C(C), .D(D), .g(g));
  e e_1 (.A(A), .B(B), .C(C), .D(D), .e(e));
  sin sin_1 (.A(A), .B(B), .C(C), .D(D), .sin(sin));
endmodule

module Circuito (
  input  A,
  input  B,
  input  C,
  input  D
);

  wire decodificador_1_a_2, decodificador_1_b_2, decodificador_1_c_2, decodificador_1_d_2, decodificador_1_e,
       decodificador_1_f, decodificador_1_g, decodificador_1_sin;

  Decodificador decodificador_1 (
    .A(A), .B(B), .C(C), .D(D), .a_2(decodificador_1_a_2), .b_2(decodificador_1_b_2),
    .c_2(decodificador_1_c_2), .d_2(decodificador_1_d_2), .e(decodificador_1_e), .f(decodificador_1_f),
    .g(decodificador_1_g), .sin(decodificador_1_sin));
  _7_Segment_Display u_7_segment_display_1 (.g(decodificador_1_sin));  // open: f, a, b, e, d, c, dp
  _7_Segment_Display u_7_segment_display_2 (
    .g(decodificador_1_g), .f(decodificador_1_b_2), .a(decodificador_1_a_2), .b(decodificador_1_f),
    .e(decodificador_1_c_2), .d(decodificador_1_d_2), .c(decodificador_1_e));  // open: dp
endmodule
