// Logisim project Logisin.circ as structural Verilog: 16 circuits, main circuit decodificador
module decodificador (
  input  A,
  input  B,
  input  C,
  input  D,
  output b_2,
  output c_2,
  output d_2,
  output e,
  output f,
  output g,
  output a_2,
  output sin
);

  wire and_1_out, and_2_out, and_3_out, and_4_out, and_5_out, not_1_out, not_2_out, not_3_out, not_4_out;

  not not_1 (not_1_out, B);
  not not_2 (not_2_out, A);
  not not_3 (not_3_out, C);
  not not_4 (not_4_out, D);
  and and_1 (and_1_out, A, not_1_out);
  and and_2 (and_2_out, C, not_4_out);
  and and_3 (and_3_out, not_1_out, not_4_out);
  and and_4 (and_4_out, not_2_out, C);
  and and_5 (and_5_out, B, not_3_out, D);
  or or_1 (a_2, and_1_out, and_2_out, and_3_out, and_4_out, and_5_out);
endmodule

module principal (
  input  A,
  input  B,
  input  C,
  input  D
);

  wire decodificador_1_a_2;

  decodificador decodificador_1 (
    .A(A), .B(B), .C(C), .D(D), .a_2(decodificador_1_a_2));  // open: b_2, c_2, d_2, e, f, g, sin
  _7_Segment_Display u_7_segment_display_1 ();  // open: g, f, a, b, e, d, c, dp
  _7_Segment_Display u_7_segment_display_2 (.a(decodificador_1_a_2));  // open: g, f, b, e, d, c, dp
endmodule

module Decodificador__B (
  input  A,
  input  B,
  input  C,
  input  D,
  output B_2
);

  wire and_1_out, and_2_out, and_3_out, and_4_out, not_1_out, not_2_out, not_3_out, not_4_out;

  not not_1 (not_1_out, B);
  not not_2 (not_2_out, A);
  not not_3 (not_3_out, D);
  not not_4 (not_4_out, C);
  and and_1 (and_1_out, not_4_out, not_3_out);
  and and_2 (and_2_out, A, not_1_out, C);
  and and_3 (and_3_out, not_2_out, B, not_3_out);
  and and_4 (and_4_out, not_2_out, B, not_4_out);
  or or_1 (B_2, and_1_out, and_2_out, and_3_out, and_4_out);
endmodule

module B (
  input  A,
  input  B,
  input  C,
  input  D
);

  wire decodificador_b_1_b_2;

  Decodificador__B decodificador_b_1 (.A(A), .B(B), .C(C), .D(D), .B_2(decodificador_b_1_b_2));
  _7_Segment_Display u_7_segment_display_1 (.f(decodificador_b_1_b_2));  // open: g, a, b, e, d, c, dp
endmodule

module Decodificador__C (
  input  A,
  input  B,
  input  C,
  input  D,
  output C_2
);

  wire and_1_out, and_2_out, not_1_out, not_2_out, not_3_out, not_4_out;

  not not_1 (not_1_out, A);
  not not_2 (not_2_out, B);
  not not_3 (not_3_out, D);
  not not_4 (not_4_out, C);
  and and_1 (and_1_out, not_2_out, not_4_out, not_3_out);
  and and_2 (and_2_out, C, not_3_out);
  or or_1 (C_2, and_1_out, and_2_out);
endmodule

module C (
  input  A,
  input  B,
  input  C,
  input  D
);

  wire decodificador_c_1_c_2;

  Decodificador__C decodificador_c_1 (.A(A), .B(B), .C(C), .D(D), .C_2(decodificador_c_1_c_2));
  _7_Segment_Display u_7_segment_display_1 (.e(decodificador_c_1_c_2));  // open: g, f, a, b, d, c, dp
endmodule

module Decodificador__D (
  input  A,
  input  B,
  input  C,
  input  D,
  output D_2
);

  wire and_1_out, and_2_out, and_3_out, and_4_out, not_1_out, not_2_out, not_3_out, not_4_out;

  not not_1 (not_1_out, A);
  not not_2 (not_2_out, B);
  not not_3 (not_3_out, D);
  not not_4 (not_4_out, C);
  and and_1 (and_1_out, not_2_out, not_4_out, not_3_out);
  and and_2 (and_2_out, B, not_4_out, D);
  and and_3 (and_3_out, not_2_out, C, D);
  and and_4 (and_4_out, C, not_3_out);
  or or_1 (D_2, and_1_out, and_2_out, and_3_out, and_4_out);
endmodule

module D (
  input  A,
  input  B,
  input  C,
  input  D
);

  wire decodificador_d_1_d_2;

  Decodificador__D decodificador_d_1 (.A(A), .B(B), .C(C), .D(D), .D_2(decodificador_d_1_d_2));
  _7_Segment_Display u_7_segment_display_1 (.d(decodificador_d_1_d_2));  // open: g, f, a, b, e, c, dp
endmodule

module Decodificador__E (
  input  A,
  input  B,
  input  C,
  input  D,
  output E
);

  wire and_1_out, and_2_out, and_3_out, and_4_out, and_5_out, not_1_out, not_2_out, not_3_out, not_4_out;

  not not_1 (not_1_out, A);
  not not_2 (not_2_out, B);
  not not_3 (not_3_out, C);
  not not_4 (not_4_out, D);
  and and_1 (and_1_out, not_3_out, not_4_out);
  and and_2 (and_2_out, not_3_out, D);
  and and_3 (and_3_out, C, D);
  and and_4 (and_4_out, not_1_out, B);
  and and_5 (and_5_out, A, not_2_out);
  or or_1 (E, and_1_out, and_2_out, and_3_out, and_4_out, and_5_out);
endmodule

module E (
  input  A,
  input  B,
  input  C,
  input  D
);

  wire decodificador_e_1_e;

  Decodificador__E decodificador_e_1 (.A(A), .B(B), .C(C), .D(D), .E(decodificador_e_1_e));
  _7_Segment_Display u_7_segment_display_1 (.c(decodificador_e_1_e));  // open: g, f, a, b, e, d, dp
endmodule

module Decodificador__F (
  input  A,
  input  B,
  input  C,
  input  D,
  output F
);

  wire and_1_out, and_2_out, and_3_out, and_4_out, and_5_out, not_1_out, not_2_out, not_3_out, not_4_out;

  not not_1 (not_1_out, B);
  not not_2 (not_2_out, A);
  not not_3 (not_3_out, C);
  not not_4 (not_4_out, D);
  and and_1 (and_1_out, not_3_out, not_4_out);
  and and_2 (and_2_out, not_2_out, not_1_out);
  and and_3 (and_3_out, A, B);
  and and_4 (and_4_out, not_3_out, D);
  and and_5 (and_5_out, C, D, not_2_out);
  or or_1 (F, and_1_out, and_2_out, and_3_out, and_4_out, and_5_out);
endmodule

module F (
  input  A,
  input  B,
  input  C,
  input  D
);

  wire decodificador_f_1_f;

  Decodificador__F decodificador_f_1 (.A(A), .B(B), .C(C), .D(D), .F(decodificador_f_1_f));
  _7_Segment_Display u_7_segment_display_1 (.b(decodificador_f_1_f));  // open: g, f, a, e, d, c, dp
endmodule

module Decodificador__G (
  input  A,
  input  B,
  input  C,
  input  D,
  output G
);

  wire and_1_out, and_2_out, and_3_out, and_4_out, not_1_out, not_2_out, not_3_out, not_4_out;

  not not_1 (not_1_out, A);
  not not_2 (not_2_out, B);
  not not_3 (not_3_out, C);
  not not_4 (not_4_out, D);
  and and_1 (and_1_out, not_3_out, B);
  and and_2 (and_2_out, A, not_4_out);
  and and_3 (and_3_out, C, not_2_out);
  and and_4 (and_4_out, C, not_4_out);
  or or_1 (G, and_1_out, and_2_out, and_3_out, and_4_out);
endmodule

module G (
  input  A,
  input  B,
  input  C,
  input  D
);

  wire decodificador_g_1_g;

  Decodificador__G decodificador_g_1 (.A(A), .B(B), .C(C), .D(D), .G(decodificador_g_1_g));
  _7_Segment_Display u_7_segment_display_1 (.g(decodificador_g_1_g));  // open: f, a, b, e, d, c, dp
endmodule

module Decodificador__Sin (
  input  A,
  input  B,
  input  C,
  input  D,
  output Sin
);

  wire and_1_out, and_2_out, and_3_out, and_4_out, not_1_out, not_2_out, not_3_out, not_4_out;

  not not_1 (not_1_out, A);
  not not_2 (not_2_out, B);
  not not_3 (not_3_out, C);
  not not_4 (not_4_out, D);
  and and_1 (and_1_out, not_3_out, B);
  and and_2 (and_2_out, A, not_4_out);
  and and_3 (and_3_out, C, not_2_out);
  and and_4 (and_4_out, C, not_4_out);
  or or_1 (Sin, and_1_out, and_2_out, and_3_out, and_4_out);
endmodule

module Sin (
  input  A,
  input  B,
  input  C,
  input  D
);

  wire decodificador_sin_1_sin;

  Decodificador__Sin decodificador_sin_1 (.A(A), .B(B), .C(C), .D(D), .Sin(decodificador_sin_1_sin));
  _7_Segment_Display u_7_segment_display_1 (.g(decodificador_sin_1_sin));  // open: f, a, b, e, d, c, dp
endmodule
