// Logisim project Trab2.Update.circ as structural Verilog: 17 circuits, main circuit Decodificador(A)
module Decodificador_A (
  input  A,
  input  B,
  input  C,
  input  D,
  output A_2
);

  wire and_1_out, and_2_out, and_3_out, and_4_out, and_5_out, not_1_out, not_2_out, not_3_out, not_4_out;

  not not_1 (not_1_out, A);
  not not_2 (not_2_out, C);
  not not_3 (not_3_out, B);
  not not_4 (not_4_out, D);
  and and_1 (and_1_out, A, not_3_out);
  and and_2 (and_2_out, C, not_4_out);
  and and_3 (and_3_out, not_3_out, not_4_out);
  and and_4 (and_4_out, not_1_out, C);
  and and_5 (and_5_out, B, not_2_out, D);
  or or_1 (A_2, and_1_out, and_2_out, and_3_out, and_4_out, and_5_out);
endmodule

module A (
  input  A,
  input  B,
  input  C,
  input  D
);

  wire decodificador_a_1_a_2;

  Decodificador_A decodificador_a_1 (.A(A), .B(B), .C(C), .D(D), .A_2(decodificador_a_1_a_2));
  _7_Segment_Display u_7_segment_display_1 ();  // open: g, f, a, b, e, d, c, dp
  _7_Segment_Display u_7_segment_display_2 (.a(decodificador_a_1_a_2));  // open: g, f, b, e, d, c, dp
endmodule

module Decodificador_B (
  input  A,
  input  B,
  input  C,
  input  D,
  output B_2
);

  wire and_1_out, and_2_out, and_3_out, and_4_out, not_1_out, not_2_out, not_3_out, not_4_out;

  not not_1 (not_1_out, A);
  not not_2 (not_2_out, C);
  not not_3 (not_3_out, B);
  not not_4 (not_4_out, D);
  and and_1 (and_1_out, not_2_out, not_4_out);
  and and_2 (and_2_out, not_1_out, B, not_2_out);
  and and_3 (and_3_out, not_1_out, B, not_4_out);
  and and_4 (and_4_out, A, not_3_out, C);
  or or_1 (B_2, and_1_out, and_2_out, and_3_out, and_4_out);
endmodule

module B (
  input  A,
  input  B,
  input  C,
  input  D
);

  wire decodificador_b_1_b_2;

  Decodificador_B decodificador_b_1 (.A(A), .B(B), .C(C), .D(D), .B_2(decodificador_b_1_b_2));
  _7_Segment_Display u_7_segment_display_1 ();  // open: g, f, a, b, e, d, c, dp
  _7_Segment_Display u_7_segment_display_2 (.f(decodificador_b_1_b_2));  // open: g, a, b, e, d, c, dp
endmodule

module Decodificador_C (
  input  A,
  input  B,
  input  C,
  input  D,
  output C_2
);

  wire and_1_out, and_2_out, not_1_out, not_2_out, not_3_out, not_4_out;

  not not_1 (not_1_out, A);
  not not_2 (not_2_out, C);
  not not_3 (not_3_out, B);
  not not_4 (not_4_out, D);
  and and_1 (and_1_out, C, not_4_out);
  and and_2 (and_2_out, not_3_out, not_4_out);
  or or_1 (C_2, and_1_out, and_2_out);
endmodule

module C (
  input  A,
  input  B,
  input  C,
  input  D
);

  wire decodificador_c_1_c_2;

  Decodificador_C decodificador_c_1 (.A(A), .B(B), .C(C), .D(D), .C_2(decodificador_c_1_c_2));
  _7_Segment_Display u_7_segment_display_1 ();  // open: g, f, a, b, e, d, c, dp
  _7_Segment_Display u_7_segment_display_2 (.e(decodificador_c_1_c_2));  // open: g, f, a, b, d, c, dp
endmodule

module Decodificador_D (
  input  A,
  input  B,
  input  C,
  input  D,
  output D_2
);

  wire and_1_out, and_2_out, and_3_out, and_4_out, not_1_out, not_2_out, not_3_out, not_4_out;

  not not_1 (not_1_out, A);
  not not_2 (not_2_out, B);
  not not_3 (not_3_out, C);
  not not_4 (not_4_out, D);
  and and_1 (and_1_out, C, not_4_out);
  and and_2 (and_2_out, not_2_out, not_4_out);
  and and_3 (and_3_out, not_2_out, C);
  and and_4 (and_4_out, B, not_3_out, D);
  or or_1 (D_2, and_1_out, and_2_out, and_3_out, and_4_out);
endmodule

module D (
  input  A,
  input  B,
  input  C,
  input  D
);

  wire decodificador_d_1_d_2;

  Decodificador_D decodificador_d_1 (.A(A), .B(B), .C(C), .D(D), .D_2(decodificador_d_1_d_2));
  _7_Segment_Display u_7_segment_display_1 ();  // open: g, f, a, b, e, d, c, dp
  _7_Segment_Display u_7_segment_display_2 (.d(decodificador_d_1_d_2));  // open: g, f, a, b, e, c, dp
endmodule

module Decodificador_E (
  input  A,
  input  B,
  input  C,
  input  D,
  output E
);

  wire and_1_out, and_2_out, and_3_out, and_4_out, not_1_out, not_2_out, not_3_out, not_4_out;

  not not_1 (not_1_out, A);
  not not_2 (not_2_out, C);
  not not_3 (not_3_out, B);
  not not_4 (not_4_out, D);
  buf and_1 (and_1_out, not_2_out);  // AND_Gate
  buf and_2 (and_2_out, D);  // AND_Gate
  and and_3 (and_3_out, not_1_out, B);
  and and_4 (and_4_out, A, not_3_out);
  or or_1 (E, and_1_out, and_2_out, and_3_out, and_4_out);
endmodule

module E (
  input  A,
  input  B,
  input  C,
  input  D
);

  wire decodificador_e_1_e;

  Decodificador_E decodificador_e_1 (.A(A), .B(B), .C(C), .D(D), .E(decodificador_e_1_e));
  _7_Segment_Display u_7_segment_display_1 ();  // open: g, f, a, b, e, d, c, dp
  _7_Segment_Display u_7_segment_display_2 (.c(decodificador_e_1_e));  // open: g, f, a, b, e, d, dp
endmodule

module Decodificador_F (
  input  A,
  input  B,
  input  C,
  input  D,
  output F
);

  wire and_1_out, and_2_out, and_3_out, and_4_out, and_5_out, not_1_out, not_2_out, not_3_out, not_4_out;

  not not_1 (not_1_out, A);
  not not_2 (not_2_out, B);
  not not_3 (not_3_out, C);
  not not_4 (not_4_out, D);
  and and_1 (and_1_out, not_3_out, not_4_out);
  and and_2 (and_2_out, A, not_3_out);
  and and_3 (and_3_out, A, B);
  and and_4 (and_4_out, not_1_out, not_2_out);
  and and_5 (and_5_out, not_1_out, C, D);
  or or_1 (F, and_1_out, and_2_out, and_3_out, and_4_out, and_5_out);
endmodule

module F (
  input  A,
  input  B,
  input  C,
  input  D
);

  wire decodificador_f_1_f;

  Decodificador_F decodificador_f_1 (.A(A), .B(B), .C(C), .D(D), .F(decodificador_f_1_f));
  _7_Segment_Display u_7_segment_display_1 ();  // open: g, f, a, b, e, d, c, dp
  _7_Segment_Display u_7_segment_display_2 (.b(decodificador_f_1_f));  // open: g, f, a, e, d, c, dp
endmodule

module Decodificador_G (
  input  A,
  input  B,
  input  C,
  input  D,
  output G
);

  wire and_1_out, and_2_out, and_3_out, and_4_out, not_1_out, not_2_out, not_3_out, not_4_out;

  not not_1 (not_1_out, A);
  not not_2 (not_2_out, C);
  not not_3 (not_3_out, B);
  not not_4 (not_4_out, D);
  and and_1 (and_1_out, C, not_4_out);
  and and_2 (and_2_out, not_3_out, C);
  and and_3 (and_3_out, B, not_2_out);
  and and_4 (and_4_out, A, not_4_out);
  or or_1 (G, and_1_out, and_2_out, and_3_out, and_4_out);
endmodule

module G (
  input  A,
  input  B,
  input  C,
  input  D
);

  wire decodificador_g_1_g;

  Decodificador_G decodificador_g_1 (.A(A), .B(B), .C(C), .D(D), .G(decodificador_g_1_g));
  _7_Segment_Display u_7_segment_display_1 (.g(decodificador_g_1_g));  // open: f, a, b, e, d, c, dp
  _7_Segment_Display u_7_segment_display_2 ();  // open: g, f, a, b, e, d, c, dp
endmodule

module Decodificador_SIN (
  input  A,
  input  B,
  input  C,
  input  D,
  output SIN
);

  wire and_1_out, and_2_out, and_3_out, and_4_out, not_1_out, not_2_out, not_3_out, not_4_out;

  not not_1 (not_1_out, A);
  not not_2 (not_2_out, B);
  not not_3 (not_3_out, C);
  not not_4 (not_4_out, D);
  and and_1 (and_1_out, C, not_4_out);
  and and_2 (and_2_out, not_2_out, C);
  and and_3 (and_3_out, B, not_3_out);
  and and_4 (and_4_out, A, not_4_out);
  or or_1 (SIN, and_1_out, and_2_out, and_3_out, and_4_out);
endmodule

module SIN (
  input  A,
  input  B,
  input  C,
  input  D
);

  wire decodificador_g_1_g;

  Decodificador_G decodificador_g_1 (.A(A), .B(B), .C(C), .D(D), .G(decodificador_g_1_g));
  _7_Segment_Display u_7_segment_display_1 (.g(decodificador_g_1_g));  // open: f, a, b, e, d, c, dp
  _7_Segment_Display u_7_segment_display_2 ();  // open: g, f, a, b, e, d, c, dp
endmodule

module main (
  input  A,
  input  B,
  input  C,
  input  D
);

  wire decodificador_a_1_a_2, decodificador_b_1_b_2, decodificador_c_1_c_2, decodificador_d_1_d_2,
       decodificador_e_1_e, decodificador_f_1_f, decodificador_sin_1_sin;

  Decodificador_A decodificador_a_1 (.A(A), .B(B), .C(C), .D(D), .A_2(decodificador_a_1_a_2));
  Decodificador_B decodificador_b_1 (.A(A), .B(B), .C(C), .D(D), .B_2(decodificador_b_1_b_2));
  Decodificador_C decodificador_c_1 (.A(A), .B(B), .C(C), .D(D), .C_2(decodificador_c_1_c_2));
  Decodificador_D decodificador_d_1 (.A(A), .B(B), .C(C), .D(D), .D_2(decodificador_d_1_d_2));
  Decodificador_E decodificador_e_1 (.A(A), .B(B), .C(C), .D(D), .E(decodificador_e_1_e));
  Decodificador_F decodificador_f_1 (.A(A), .B(B), .C(C), .D(D), .F(decodificador_f_1_f));
  Decodificador_SIN decodificador_sin_1 (.A(A), .B(B), .C(C), .D(D), .SIN(decodificador_sin_1_sin));
  _7_Segment_Display u_7_segment_display_1 (.g(A));  // open: f, a, b, e, d, c, dp
  _7_Segment_Display u_7_segment_display_2 (
    .g(decodificador_sin_1_sin), .f(decodificador_b_1_b_2), .a(decodificador_a_1_a_2),
    .b(decodificador_f_1_f), .e(decodificador_c_1_c_2), .d(decodificador_d_1_d_2), .c(decodificador_e_1_e));  // open: dp
endmodule
