// Logisim project TRAB2022.circ as structural Verilog: 2 circuits, main circuit main
module main (
  input  A,
  input  B,
  input  C,
  input  D,
  output A_2,
  output B_2,
  output C_2,
  output D_2,
  output E,
  output F,
  output G,
  output H
);

  wire and_1_out, and_2_out, and_3_out, and_4_out, and_5_out, and_6_out, and_7_out, and_8_out, and_9_out,
       and_10_out, and_11_out, and_12_out, and_13_out, and_14_out, and_15_out, and_16_out, and_17_out,
       and_18_out, and_19_out, and_20_out, and_21_out, and_22_out, and_23_out, and_24_out, and_25_out,
       and_26_out, and_27_out, and_28_out, and_29_out, and_30_out, and_31_out, and_32_out, and_33_out,
       and_34_out, and_35_out, and_36_out, not_1_out, not_2_out, not_3_out, not_4_out;

  not not_1 (not_1_out, A);
  not not_2 (not_2_out, C);
  not not_3 (not_3_out, B);
  not not_4 (not_4_out, D);
  and and_1 (and_1_out, A, not_3_out);
  and and_2 (and_2_out, C, not_4_out);
  and and_3 (and_3_out, not_3_out, not_4_out);
  and and_4 (and_4_out, not_1_out, C);
  and and_5 (and_5_out, B, not_2_out, D);
  and and_6 (and_6_out, not_2_out, not_4_out);
  and and_7 (and_7_out, A, not_2_out, C);
  and and_8 (and_8_out, not_1_out, B, not_4_out);
  and and_9 (and_9_out, not_1_out, B, not_2_out);
  and and_10 (and_10_out, not_3_out, not_4_out);
  and and_11 (and_11_out, C, not_4_out);
  and and_12 (and_12_out, not_1_out, not_3_out, C);
  and and_13 (and_13_out, not_1_out, not_3_out, not_4_out);
  and and_14 (and_14_out, A, not_3_out, not_4_out);
  and and_15 (and_15_out, C, not_4_out);
  and and_16 (and_16_out, B, not_2_out);
  and and_17 (and_17_out, A, not_3_out, C);
  and and_18 (and_18_out, not_1_out, not_2_out);
  and and_19 (and_19_out, not_3_out, C, D);
  and and_20 (and_20_out, not_1_out, B, C);
  and and_21 (and_21_out, B, C, D);
  and and_22 (and_22_out, A, not_3_out, C);
  and and_23 (and_23_out, A, not_2_out);
  and and_24 (and_24_out, not_1_out, not_3_out);
  and and_25 (and_25_out, B, C, D);
  and and_26 (and_26_out, A, B, D);
  and and_27 (and_27_out, A, C, not_4_out);
  and and_28 (and_28_out, not_1_out, not_2_out, not_4_out);
  and and_29 (and_29_out, A, not_3_out, not_2_out);
  and and_30 (and_30_out, not_1_out, not_3_out, C);
  and and_31 (and_31_out, not_1_out, B, not_4_out);
  and and_32 (and_32_out, A, not_3_out, C);
  and and_33 (and_33_out, B, not_2_out, D);
  and and_34 (and_34_out, A, not_2_out, not_4_out);
  and and_35 (and_35_out, A, B);
  and and_36 (and_36_out, A, not_3_out);
  or or_1 (C_2, and_10_out, and_11_out);
  or or_2 (G, and_30_out, and_31_out, and_32_out, and_33_out, and_34_out);
  or or_3 (H, and_35_out, and_36_out);
  or or_4 (A_2, and_1_out, and_2_out, and_3_out, and_4_out, and_5_out);
  or or_5 (B_2, and_6_out, and_7_out, and_8_out, and_9_out);
  or or_6 (D_2, and_12_out, and_13_out, and_14_out, and_15_out, and_16_out, and_17_out);
  or or_7 (E, and_18_out, and_19_out, and_20_out, and_21_out, and_22_out, and_23_out);
  or or_8 (F, and_24_out, and_25_out, and_26_out, and_27_out, and_28_out, and_29_out);
endmodule

module MAIN (
  input  in_1,
  input  in_2,
  input  in_3,
  input  in_4,
  input  in_5,
  input  in_6,
  input  in_7,
  input  in_8,
  input  in_9,
  input  in_10,
  input  in_11,
  input  in_12,
  input  in_13,
  input  in_14,
  input  in_15,
  input  in_16,
  input  in_17,
  input  in_18,
  input  in_19,
  input  in_20,
  input  in_21,
  input  in_22,
  input  in_23,
  input  in_24,
  input  in_25,
  input  in_26,
  input  in_27,
  input  in_28,
  input  in_29,
  input  in_30,
  input  in_31,
  input  in_32,
  input  in_33,
  input  in_34,
  input  in_35,
  input  in_36,
  input  in_37,
  input  in_38,
  input  in_39,
  input  in_40,
  input  in_41,
  input  in_42,
  input  in_43,
  input  in_44,
  input  in_45,
  input  in_46,
  input  in_47,
  input  in_48,
  input  in_49,
  input  in_50,
  input  in_51,
  input  in_52,
  input  in_53,
  input  in_54,
  input  in_55,
  input  in_56,
  input  in_57,
  input  in_58,
  input  in_59,
  input  in_60
);

  wire main_1_a_2, main_1_f, main_2_a_2, main_2_b_2, main_2_c_2, main_2_e, main_2_f, main_3_a_2, main_3_b_2,
       main_3_c_2, main_3_e, main_3_f, main_4_a_2, main_4_b_2, main_4_c_2, main_4_f, main_5_a_2, main_5_b_2,
       main_5_c_2, main_5_d_2, main_5_e, main_5_f, main_6_a_2, main_6_b_2, main_6_c_2, main_6_e, main_6_f,
       main_7_a_2, main_7_b_2, main_7_c_2, main_7_d_2, main_7_e, main_7_f, main_8_b_2, main_8_c_2, main_8_f,
       main_9_a_2, main_9_e, main_9_f, main_10_a_2, main_10_e, main_10_f, main_11_a_2, main_11_f,
       main_12_a_2, main_12_b_2, main_12_e, main_12_f, main_13_b_2, main_13_c_2, main_13_f, main_14_a_2,
       main_14_d_2, main_14_f, main_15_a_2, main_15_f;

  main main_1 (
    .A(in_21), .B(in_22), .C(in_23), .D(in_24), .A_2(main_1_a_2), .F(main_1_f));  // open: B_2, C_2, D_2, E, G, H
  main main_2 (
    .A(in_25), .B(in_26), .C(in_27), .D(in_28), .A_2(main_2_a_2), .B_2(main_2_b_2), .C_2(main_2_c_2),
    .E(main_2_e), .F(main_2_f));  // open: D_2, G, H
  main main_3 (
    .A(in_37), .B(in_38), .C(in_39), .D(in_40), .A_2(main_3_a_2), .B_2(main_3_b_2), .C_2(main_3_c_2),
    .E(main_3_e), .F(main_3_f));  // open: D_2, G, H
  main main_4 (
    .A(in_49), .B(in_50), .C(in_51), .D(in_52), .A_2(main_4_a_2), .B_2(main_4_b_2), .C_2(main_4_c_2),
    .F(main_4_f));  // open: D_2, E, G, H
  main main_5 (
    .A(in_1), .B(in_2), .C(in_3), .D(in_4), .A_2(main_5_a_2), .B_2(main_5_b_2), .C_2(main_5_c_2),
    .D_2(main_5_d_2), .E(main_5_e), .F(main_5_f));  // open: G, H
  _7_Segment_Display u_7_segment_display_1 ();  // open: g, f, a, b, e, d, c, dp
  _7_Segment_Display u_7_segment_display_2 ();  // open: g, f, a, b, e, d, c, dp
  _7_Segment_Display u_7_segment_display_3 ();  // open: g, f, a, b, e, d, c, dp
  _7_Segment_Display u_7_segment_display_4 ();  // open: g, f, a, b, e, d, c, dp
  _7_Segment_Display u_7_segment_display_5 ();  // open: g, f, a, b, e, d, c, dp
  _7_Segment_Display u_7_segment_display_6 (
    .f(main_5_c_2), .a(main_5_b_2), .b(main_5_a_2), .e(main_5_d_2), .d(main_5_e), .c(main_5_f));  // open: g, dp
  _7_Segment_Display u_7_segment_display_7 (.b(main_1_a_2), .c(main_1_f));  // open: g, f, a, e, d, dp
  _7_Segment_Display u_7_segment_display_8 (
    .g(main_2_c_2), .a(main_2_b_2), .b(main_2_a_2), .e(main_2_e), .d(main_2_f));  // open: f, c, dp
  _7_Segment_Display u_7_segment_display_9 (
    .g(main_3_c_2), .a(main_3_b_2), .b(main_3_a_2), .d(main_3_e), .c(main_3_f));  // open: f, e, dp
  _7_Segment_Display u_7_segment_display_10 (
    .g(main_4_c_2), .f(main_4_b_2), .b(main_4_a_2), .c(main_4_f));  // open: a, e, d, dp
  main main_6 (
    .A(in_5), .B(in_6), .C(in_7), .D(in_8), .A_2(main_6_a_2), .B_2(main_6_b_2), .C_2(main_6_c_2),
    .E(main_6_e), .F(main_6_f));  // open: D_2, G, H
  main main_7 (
    .A(in_13), .B(in_14), .C(in_15), .D(in_16), .A_2(main_7_a_2), .B_2(main_7_b_2), .C_2(main_7_c_2),
    .D_2(main_7_d_2), .E(main_7_e), .F(main_7_f));  // open: G, H
  main main_8 (
    .A(in_33), .B(in_34), .C(in_35), .D(in_36), .B_2(main_8_b_2), .C_2(main_8_c_2), .F(main_8_f));  // open: A_2, D_2, E, G, H
  main main_9 (
    .A(in_45), .B(in_46), .C(in_47), .D(in_48), .A_2(main_9_a_2), .E(main_9_e), .F(main_9_f));  // open: B_2, C_2, D_2, G, H
  main main_10 (
    .A(in_53), .B(in_54), .C(in_55), .D(in_56), .A_2(main_10_a_2), .E(main_10_e), .F(main_10_f));  // open: B_2, C_2, D_2, G, H
  _7_Segment_Display u_7_segment_display_11 ();  // open: g, f, a, b, e, d, c, dp
  _7_Segment_Display u_7_segment_display_12 ();  // open: g, f, a, b, e, d, c, dp
  _7_Segment_Display u_7_segment_display_13 ();  // open: g, f, a, b, e, d, c, dp
  _7_Segment_Display u_7_segment_display_14 (.g(main_9_e));  // open: f, a, b, e, d, c, dp
  _7_Segment_Display u_7_segment_display_15 (.g(main_10_e));  // open: f, a, b, e, d, c, dp
  _7_Segment_Display u_7_segment_display_16 (
    .g(main_6_c_2), .f(main_6_b_2), .a(main_6_a_2), .d(main_6_e), .c(main_6_f));  // open: b, e, dp
  _7_Segment_Display u_7_segment_display_17 (
    .g(main_7_c_2), .f(main_7_b_2), .a(main_7_a_2), .e(main_7_d_2), .d(main_7_e), .c(main_7_f));  // open: b, dp
  _7_Segment_Display u_7_segment_display_18 (.a(main_8_c_2), .b(main_8_b_2), .c(main_8_f));  // open: g, f, e, d, dp
  _7_Segment_Display u_7_segment_display_19 (.a(main_9_a_2), .b(main_9_a_2), .c(main_9_f));  // open: g, f, e, d, dp
  _7_Segment_Display u_7_segment_display_20 (
    .g(main_10_a_2), .f(main_10_a_2), .a(main_10_a_2), .e(main_10_f), .d(main_10_f), .c(main_10_f));  // open: b, dp
  main main_11 (
    .A(in_17), .B(in_18), .C(in_19), .D(in_20), .A_2(main_11_a_2), .F(main_11_f));  // open: B_2, C_2, D_2, E, G, H
  main main_12 (
    .A(in_29), .B(in_30), .C(in_31), .D(in_32), .A_2(main_12_a_2), .B_2(main_12_b_2), .E(main_12_e),
    .F(main_12_f));  // open: C_2, D_2, G, H
  main main_13 (
    .A(in_41), .B(in_42), .C(in_43), .D(in_44), .B_2(main_13_b_2), .C_2(main_13_c_2), .F(main_13_f));  // open: A_2, D_2, E, G, H
  main main_14 (
    .A(in_57), .B(in_58), .C(in_59), .D(in_60), .A_2(main_14_a_2), .D_2(main_14_d_2), .F(main_14_f));  // open: B_2, C_2, E, G, H
  main main_15 (
    .A(in_9), .B(in_10), .C(in_11), .D(in_12), .A_2(main_15_a_2), .F(main_15_f));  // open: B_2, C_2, D_2, E, G, H
  _7_Segment_Display u_7_segment_display_21 (.g(main_15_f));  // open: f, a, b, e, d, c, dp
  _7_Segment_Display u_7_segment_display_22 (.g(main_11_f));  // open: f, a, b, e, d, c, dp
  _7_Segment_Display u_7_segment_display_23 (.g(main_12_e));  // open: f, a, b, e, d, c, dp
  _7_Segment_Display u_7_segment_display_24 (.g(main_13_c_2));  // open: f, a, b, e, d, c, dp
  _7_Segment_Display u_7_segment_display_25 (.g(main_14_d_2));  // open: f, a, b, e, d, c, dp
  _7_Segment_Display u_7_segment_display_26 (
    .g(main_15_a_2), .f(main_15_a_2), .a(main_15_a_2), .d(main_15_f), .c(main_15_f));  // open: b, e, dp
  _7_Segment_Display u_7_segment_display_27 (
    .g(main_11_a_2), .f(main_11_a_2), .b(main_11_a_2), .c(main_11_f));  // open: a, e, d, dp
  _7_Segment_Display u_7_segment_display_28 (
    .g(main_12_b_2), .a(main_12_a_2), .b(main_12_a_2), .d(main_12_f), .c(main_12_f));  // open: f, e, dp
  _7_Segment_Display u_7_segment_display_29 (
    .g(main_13_c_2), .a(main_13_c_2), .b(main_13_b_2), .e(main_13_f), .d(main_13_f));  // open: f, c, dp
  _7_Segment_Display u_7_segment_display_30 (.b(main_14_a_2), .c(main_14_f));  // open: g, f, a, e, d, dp
endmodule
