// Logisim project Atividade2.circ as structural Verilog: 2 circuits, main circuit Display
module Display (
  input  A,
  input  B,
  input  C,
  input  D
);

  wire decodificador_c_2_1_a_2, decodificador_c_2_1_b_2, decodificador_c_2_1_c_2, decodificador_c_2_1_d_2,
       decodificador_c_2_1_e, decodificador_c_2_1_f, decodificador_c_2_1_g, decodificador_c_2_1_sin;

  Decodificador_C_2 decodificador_c_2_1 (
    .A(A), .B(B), .C(C), .D(D), .a_2(decodificador_c_2_1_a_2), .b_2(decodificador_c_2_1_b_2),
    .c_2(decodificador_c_2_1_c_2), .d_2(decodificador_c_2_1_d_2), .e(decodificador_c_2_1_e),
    .f(decodificador_c_2_1_f), .g(decodificador_c_2_1_g), .sin(decodificador_c_2_1_sin));
  _7_Segment_Display u_7_segment_display_1 (
    .g(decodificador_c_2_1_g), .f(decodificador_c_2_1_b_2), .a(decodificador_c_2_1_a_2),
    .b(decodificador_c_2_1_f), .e(decodificador_c_2_1_c_2), .d(decodificador_c_2_1_d_2),
    .c(decodificador_c_2_1_e));  // open: dp
  _7_Segment_Display u_7_segment_display_2 (.g(decodificador_c_2_1_sin));  // open: f, a, b, e, d, c, dp
endmodule

// Dcodificador
module Decodificador_C_2 (
  input  A,
  input  B,
  input  C,
  input  D,
  output a_2,
  output b_2,
  output c_2,
  output d_2,
  output e,
  output f,
  output g,
  output sin
);

  wire and_1_out, and_2_out, and_3_out, and_4_out, and_5_out, and_6_out, and_7_out, and_8_out, and_9_out,
       and_10_out, and_11_out, and_12_out, and_13_out, and_14_out, and_15_out, and_16_out, and_17_out,
       and_18_out, and_19_out, and_20_out, and_21_out, and_22_out, and_23_out, and_24_out, and_25_out,
       and_26_out, not_1_out, not_2_out, not_3_out, not_4_out;

  and and_1 (and_1_out, A, not_2_out);
  not not_1 (not_1_out, A);
  not not_2 (not_2_out, B);
  not not_3 (not_3_out, C);
  not not_4 (not_4_out, D);
  or or_1 (a_2, and_1_out, and_3_out, and_2_out, and_5_out, and_4_out);
  and and_2 (and_2_out, not_1_out, C);
  and and_3 (and_3_out, C, not_4_out);
  and and_4 (and_4_out, B, not_3_out, D);
  and and_5 (and_5_out, not_2_out, not_4_out);
  and and_6 (and_6_out, not_3_out, not_4_out);
  or or_2 (b_2, and_6_out, and_8_out, and_7_out, and_9_out);
  and and_7 (and_7_out, not_1_out, B, not_3_out);
  and and_8 (and_8_out, A, not_2_out, C);
  and and_9 (and_9_out, not_1_out, B, not_4_out);
  or or_3 (c_2, and_11_out, and_10_out);
  and and_10 (and_10_out, not_2_out, not_4_out);
  and and_11 (and_11_out, C, not_4_out);
  and and_12 (and_12_out, C, not_4_out);
  or or_4 (d_2, and_12_out, and_13_out, and_14_out, and_15_out);
  and and_13 (and_13_out, not_2_out, C);
  and and_14 (and_14_out, not_2_out, not_4_out);
  and and_15 (and_15_out, B, not_3_out, D);
  or or_5 (e, not_3_out, D, and_17_out, and_16_out);
  and and_16 (and_16_out, A, not_2_out);
  and and_17 (and_17_out, not_1_out, B);
  and and_18 (and_18_out, not_1_out, not_2_out);
  or or_6 (f, and_18_out, and_20_out, and_19_out, and_21_out, and_22_out);
  and and_19 (and_19_out, not_3_out, not_4_out);
  and and_20 (and_20_out, A, B);
  and and_21 (and_21_out, A, not_3_out);
  and and_22 (and_22_out, not_1_out, C, D);
  and and_23 (and_23_out, C, not_4_out);
  or or_7 (g, and_23_out, and_25_out, and_24_out, and_26_out);
  and and_24 (and_24_out, A, not_4_out);
  and and_25 (and_25_out, B, not_3_out);
  and and_26 (and_26_out, not_2_out, C);

  assign sin = A;
endmodule
