// Logisim project projeto_ativ_2.circ as structural Verilog: 2 circuits, main circuit decoder
module decoder (
  input  A,
  input  B,
  input  C,
  input  D,
  output a_2,
  output b_2,
  output c_2,
  output d_2,
  output e,
  output f,
  output g,
  output sin
);

  wire and_1_out, and_2_out, and_3_out, and_4_out, and_5_out, and_6_out, and_7_out, and_8_out, and_9_out,
       and_10_out, and_11_out, and_12_out, and_13_out, and_14_out, and_15_out, and_16_out, and_17_out,
       and_18_out, and_19_out, not_1_out, not_2_out, not_3_out, not_4_out;

  not not_1 (not_1_out, A);
  not not_2 (not_2_out, B);
  not not_3 (not_3_out, C);
  not not_4 (not_4_out, D);
  and and_1 (and_1_out, not_2_out, A);
  and and_2 (and_2_out, not_4_out, C);
  and and_3 (and_3_out, not_2_out, not_4_out);
  and and_4 (and_4_out, C, not_1_out);
  and and_5 (and_5_out, D, not_3_out, B);
  and and_6 (and_6_out, not_2_out, C, D);
  or or_1 (a_2, and_1_out, and_2_out, and_3_out, and_4_out, and_5_out);
  and and_7 (and_7_out, not_3_out, not_4_out);
  and and_8 (and_8_out, A, not_2_out, C);
  and and_9 (and_9_out, not_1_out, B, not_3_out);
  and and_10 (and_10_out, not_1_out, B, not_4_out);
  and and_11 (and_11_out, not_1_out, B);
  and and_12 (and_12_out, A, B);
  and and_13 (and_13_out, A, not_3_out);
  and and_14 (and_14_out, not_1_out, not_2_out);
  and and_15 (and_15_out, B, C, D);
  and and_16 (and_16_out, B, not_3_out);
  and and_17 (and_17_out, A, not_4_out);
  and and_18 (and_18_out, C, not_4_out);
  and and_19 (and_19_out, not_2_out, C);
  or or_2 (c_2, and_3_out, and_2_out);
  or or_3 (d_2, and_3_out, and_5_out, and_2_out, and_6_out);
  or or_4 (b_2, and_7_out, and_8_out, and_9_out, and_10_out);
  or or_5 (e, not_3_out, D, and_1_out, and_11_out);
  or or_6 (g, and_16_out, and_17_out, and_18_out, and_19_out);
  or or_7 (f, and_12_out, and_13_out, and_14_out, and_15_out, and_7_out);

  assign sin = A;
endmodule

module main (
  input  A,
  input  B,
  input  C,
  input  D
);

  wire decoder_1_a_2, decoder_1_b_2, decoder_1_c_2, decoder_1_d_2, decoder_1_e, decoder_1_f, decoder_1_g,
       decoder_1_sin;

  decoder decoder_1 (
    .A(A), .B(B), .C(C), .D(D), .a_2(decoder_1_a_2), .b_2(decoder_1_b_2), .c_2(decoder_1_c_2),
    .d_2(decoder_1_d_2), .e(decoder_1_e), .f(decoder_1_f), .g(decoder_1_g), .sin(decoder_1_sin));
  _7_Segment_Display u_7_segment_display_1 (.g(decoder_1_sin));  // open: f, a, b, e, d, c, dp
  _7_Segment_Display u_7_segment_display_2 (
    .g(decoder_1_g), .f(decoder_1_b_2), .a(decoder_1_a_2), .b(decoder_1_f), .e(decoder_1_c_2),
    .d(decoder_1_d_2), .c(decoder_1_e));  // open: dp
endmodule
