// Logisim project PROJETO_rafaelffoppa (1) - Copia.circ as structural Verilog: 9 circuits, main circuit A
module A (
  input  a,
  input  b,
  input  c,
  input  d,
  output a_2
);

  wire and_1_out, and_2_out, and_3_out, and_4_out, and_5_out, not_1_out, not_2_out, not_3_out, not_4_out;

  not not_1 (not_1_out, a);
  not not_2 (not_2_out, b);
  not not_3 (not_3_out, c);
  not not_4 (not_4_out, d);
  and and_1 (and_1_out, a, not_2_out);
  and and_2 (and_2_out, c, not_4_out);
  and and_3 (and_3_out, not_2_out, not_4_out);
  and and_4 (and_4_out, not_1_out, c);
  and and_5 (and_5_out, b, not_3_out, d);
  or or_1 (a_2, and_1_out, and_2_out, and_3_out, and_4_out, and_5_out);
endmodule

module B (
  input  a,
  input  b,
  input  c,
  input  d,
  output B_2
);

  wire and_1_out, and_2_out, and_3_out, and_4_out, not_2_out, not_3_out, not_4_out;

  not not_1 (a, a);
  not not_2 (not_2_out, b);
  not not_3 (not_3_out, c);
  not not_4 (not_4_out, d);
  and and_1 (and_1_out, a, b, not_3_out);
  and and_2 (and_2_out, not_3_out, not_4_out);
  and and_3 (and_3_out, a, b, not_4_out);
  and and_4 (and_4_out, a, not_2_out, c);
  or or_1 (B_2, and_1_out, and_2_out, and_3_out, and_4_out);
endmodule

module C (
  input  b,
  input  c,
  input  d,
  output C_2
);

  wire and_1_out, and_2_out, not_1_out, not_2_out;

  not not_1 (not_1_out, b);
  not not_2 (not_2_out, d);
  and and_1 (and_1_out, not_1_out, not_2_out);
  and and_2 (and_2_out, c, not_2_out);
  or or_1 (C_2, and_1_out, and_2_out);
endmodule

module D (
  input  a,
  input  b,
  input  c,
  output D
);

  wire and_1_out, not_1_out, not_2_out;

  not not_1 (not_1_out, b);
  not not_2 (not_2_out, a);
  and and_1 (and_1_out, c, not_1_out, not_2_out);
  or or_1 (D, and_1_out, a);
endmodule

module E (
  input  a,
  input  b,
  input  c,
  input  d,
  output E
);

  wire and_1_out, and_2_out, not_1_out, not_2_out;

  not not_1 (not_1_out, a);
  not not_2 (not_2_out, b);
  and and_1 (and_1_out, not_1_out, b);
  and and_2 (and_2_out, not_2_out, a);
  or or_1 (E, d, and_1_out, and_2_out, c);
endmodule

module F (
  input  a,
  input  b,
  input  c,
  input  d,
  output F
);

  wire and_1_out, and_2_out, and_3_out, and_4_out, and_5_out, not_1_out, not_2_out, not_3_out, not_4_out;

  not not_1 (not_1_out, a);
  not not_2 (not_2_out, b);
  not not_3 (not_3_out, c);
  not not_4 (not_4_out, d);
  and and_1 (and_1_out, not_1_out, not_2_out);
  and and_2 (and_2_out, b, c, d);
  and and_3 (and_3_out, a, b);
  and and_4 (and_4_out, a, not_3_out);
  and and_5 (and_5_out, not_3_out, not_4_out);
  or or_1 (F, and_1_out, and_2_out, and_3_out, and_4_out, and_5_out);
endmodule

module G (
  input  a,
  input  b,
  input  c,
  input  d,
  output G
);

  wire and_1_out, and_2_out, and_3_out, and_4_out, and_5_out, not_1_out, not_2_out, not_3_out, not_4_out;

  not not_1 (not_1_out, a);
  not not_2 (not_2_out, b);
  not not_3 (not_3_out, c);
  not not_4 (not_4_out, d);
  and and_1 (and_1_out, b, not_3_out);
  and and_2 (and_2_out, not_1_out, not_2_out, c);
  and and_3 (and_3_out, c, not_4_out);
  and and_4 (and_4_out, a, not_2_out, c);
  and and_5 (and_5_out, a, not_3_out, not_4_out);
  or or_1 (G, and_1_out, and_2_out, and_3_out, and_4_out, and_5_out);
endmodule

module SIN (
  input  a,
  output SIN
);


  assign SIN = a;
endmodule

module PROJETO (
  input  A,
  input  B,
  input  C,
  input  D
);

  wire a_1_a_2, b_1_b_2, c_1_c_2, d_1_d, e_1_e, f_1_f, g_1_g, sin_1_sin;

  SIN sin_1 (.a(A), .SIN(sin_1_sin));
  A a_1 (.a(A), .b(B), .c(C), .d(D), .a_2(a_1_a_2));
  B b_1 (.a(A), .b(B), .c(C), .d(D), .B_2(b_1_b_2));
  C c_1 (.b(B), .c(C), .d(D), .C_2(c_1_c_2));
  D d_1 (.a(A), .b(B), .c(C), .D(d_1_d));
  _7_Segment_Display u_7_segment_display_1 (
    .g(g_1_g), .f(b_1_b_2), .a(a_1_a_2), .b(f_1_f), .e(c_1_c_2), .d(d_1_d), .c(e_1_e));  // open: dp
  _7_Segment_Display u_7_segment_display_2 (.g(sin_1_sin));  // open: f, a, b, e, d, c, dp
  E e_1 (.a(A), .b(B), .c(C), .d(D), .E(e_1_e));
  F f_1 (.a(A), .b(B), .c(C), .d(D), .F(f_1_f));
  G g_1 (.a(A), .b(B), .c(C), .d(D), .G(g_1_g));
endmodule
