// Logisim project atividade 2.circ as structural Verilog
module decodificador (
  input  A,
  input  B,
  input  C,
  input  D,
  output a_2,
  output b_2,
  output c_2,
  output d_2,
  output e,
  output f,
  output g,
  output sin
);

  wire and_1_out, and_2_out, and_3_out, and_4_out, and_5_out, and_6_out, and_7_out, and_8_out, and_9_out,
       and_10_out, and_11_out, and_12_out, and_13_out, and_14_out, and_15_out, and_16_out, and_17_out,
       and_18_out, and_19_out, and_20_out, and_21_out, and_22_out, and_23_out, and_24_out, and_25_out,
       and_27_out, and_29_out, and_30_out, and_31_out, and_32_out, and_33_out, and_34_out, and_35_out,
       and_36_out, and_37_out, and_38_out, and_39_out, not_1_out, not_2_out, not_3_out, not_4_out;

  not not_1 (not_1_out, A);
  not not_2 (not_2_out, B);
  not not_3 (not_3_out, C);
  not not_4 (not_4_out, D);
  and and_1 (and_1_out, A, not_2_out);
  and and_2 (and_2_out, C, not_4_out);
  and and_3 (and_3_out, not_2_out, not_4_out);
  and and_4 (and_4_out, not_1_out, C);
  and and_5 (and_5_out, B, not_3_out, D);
  and and_6 (and_6_out, not_3_out, not_4_out);
  and and_7 (and_7_out, A, not_2_out, C);
  and and_8 (and_8_out, not_1_out, B, not_4_out);
  and and_9 (and_9_out, not_1_out, B, not_3_out);
  and and_10 (and_10_out, not_3_out, not_4_out);
  and and_11 (and_11_out, A, not_2_out, C);
  and and_12 (and_12_out, not_1_out, B, not_4_out);
  and and_13 (and_13_out, not_1_out, B, not_3_out);
  and and_14 (and_14_out, not_1_out, not_2_out, not_3_out);
  and and_15 (and_15_out, not_1_out, not_2_out, not_4_out);
  and and_16 (and_16_out, A, not_2_out, not_4_out);
  and and_17 (and_17_out, C, not_4_out);
  and and_18 (and_18_out, A, not_2_out, C);
  and and_19 (and_19_out, B, not_3_out, D);
  and and_20 (and_20_out, not_1_out, not_3_out);
  and and_21 (and_21_out, not_2_out, C, D);
  and and_22 (and_22_out, not_1_out, B, C);
  and and_23 (and_23_out, B, C, D);
  and and_24 (and_24_out, A, not_2_out, C);
  and and_25 (and_25_out, not_1_out, not_2_out);
  // AND_Gate and_26 is placed but not wired
  and and_27 (and_27_out, B, C, D);
  // AND_Gate and_28 is placed but not wired
  and and_29 (and_29_out, A, B, D);
  and and_30 (and_30_out, A, C, not_4_out);
  and and_31 (and_31_out, not_1_out, not_3_out, not_4_out);
  and and_32 (and_32_out, A, not_2_out, not_3_out);
  and and_33 (and_33_out, not_1_out, not_2_out, C);
  and and_34 (and_34_out, not_1_out, not_4_out);
  and and_35 (and_35_out, A, not_2_out, not_3_out);
  and and_36 (and_36_out, B, not_3_out, D);
  and and_37 (and_37_out, A, not_3_out, not_4_out);
  and and_38 (and_38_out, A, not_2_out);
  and and_39 (and_39_out, A, B);
  or or_1 (a_2, and_1_out, and_2_out, and_3_out, and_4_out, and_5_out);
  or or_2 (b_2, and_6_out, and_7_out, and_8_out, and_9_out);
  or or_3 (c_2, and_10_out, and_11_out, and_12_out, and_13_out);
  or or_4 (d_2, and_14_out, and_15_out, and_16_out, and_17_out, and_18_out, and_19_out);
  or or_5 (e, and_20_out, and_21_out, and_22_out, and_23_out, and_24_out);
  or or_6 (f, and_25_out, and_27_out, and_29_out, and_30_out, and_31_out, and_32_out);
  or or_7 (g, and_33_out, and_34_out, and_35_out, and_36_out, and_37_out);
  or or_8 (sin, and_38_out, and_39_out);
endmodule

module Principal (
  input  in_1,
  input  in_2,
  input  in_3,
  input  in_4
);

  wire decodificador_1_a_2, decodificador_1_e;

  decodificador decodificador_1 (
    .A(in_1), .B(in_2), .C(in_3), .D(in_4), .a_2(decodificador_1_a_2), .e(decodificador_1_e));  // open: b_2, c_2, d_2, f, g, sin
  _7_Segment_Display u_7_segment_display_1 ();  // open: g, f, a, b, e, d, c, dp
  _7_Segment_Display u_7_segment_display_2 (.f(decodificador_1_a_2), .a(decodificador_1_e));  // open: g, b, e, d, c, dp
endmodule
